# Fritzing sketch 3LEDs (saved by Fritzing 0.9.3b)
breadboards: 2

parts:
  Part1 = Arduino Uno (Rev3)
  J2 = single row smd female pin header, 4 pins [form="♀ (female)"]
  J1 = single row smd female pin header, 5 pins [form="♀ (female)"]
  Part2 = Bluetooth HM-11
  Part3 = Bluetooth HM-11
  LED1 = LED - 3mm [color="Green (555nm)" package="3 mm [THT]"]
  LED2 = LED - 3mm [color="Blue (430nm)" package="3 mm [THT]"]
  LED3 = LED - 3mm [color="Red (633nm)" package="3 mm [THT]"]
  R2 = Resistor [tolerance=±5% resistance=220 package=THT]
  R3 = Resistor [tolerance=±5% resistance=220 package=THT]
  R4 = Resistor [tolerance=±5% resistance=220 package=THT]

nets:
  N1: Part1.D2, Part3.UART_TX
  N2: Part1.D3_PWM, Part3.UART_RX
  N3: Part1.D4, LED3.cathode
  N4: Part1.D5_PWM, LED2.cathode
  N5: Part1.D6_PWM, LED1.cathode
  3V3: Part1.3V3, Part3.VCC
  GND: Part1.GND, Part3.GND, R2.Pin_0, R3.Pin_0, R4.Pin_0
  N6: J2.pin1, Part2.RESETB
  N7: J2.pin3, Part2.UART_TX
  N8: J2.pin4, Part2.D_DATA
  N9: J1.pin1, Part2.VCC
  N10: J1.pin2, Part2.GND
  N11: J1.pin4, Part2.UART_RX
  N12: J1.pin5, Part2.D_CLOCK
  N13: LED1.anode, R4.Pin_1
  N14: LED2.anode, R3.Pin_1
  N15: LED3.anode, R2.Pin_1

notes:
  See HM-11_connector.jpg for more indepth connector wiring details
  HM-11 Connector
  HM-11 to Arduino
  220Ω resistors
