# Fritzing sketch 3LEDs_with_LCD_output (saved by Fritzing 0.9.3b)
breadboards: 2

parts:
  Part1 = Arduino Uno (Rev3)
  J2 = single row smd female pin header, 4 pins [form="♀ (female)"]
  J1 = single row smd female pin header, 5 pins [form="♀ (female)"]
  Part2 = Bluetooth HM-11
  Part3 = Bluetooth HM-11
  LED1 = LED - 3mm [color="Green (555nm)" package="3 mm [THT]"]
  LED2 = LED - 3mm [color="Blue (430nm)" package="3 mm [THT]"]
  LED3 = LED - 3mm [color="Red (633nm)" package="3 mm [THT]"]
  R2 = Resistor [tolerance=±5% resistance=220 package=THT]
  R3 = Resistor [tolerance=±5% resistance=220 package=THT]
  R4 = Resistor [tolerance=±5% resistance=220 package=THT]
  U1 = LCD-16X2 [package=lcd-16x2]
  R5 = Resistor [tolerance=±5% resistance=220 package=THT]
  R6 = Trimmer Potentiometer [maximum_resistance=10kΩ package=THT]

nets:
  N1: Part1.D8, U1.D5
  N2: Part1.D10_PWM/SS, U1.RS
  N3: Part1.D11_PWM/MOSI, U1.E
  N4: Part1.D12/MISO, U1.D6
  N5: Part1.D13/SCK, U1.D7
  N6: Part1.D2, Part3.UART_TX
  N7: Part1.D3_PWM, Part3.UART_RX
  N8: Part1.D4, LED3.cathode
  N9: Part1.D5_PWM, LED2.cathode
  N10: Part1.D6_PWM, LED1.cathode
  N11: Part1.D7, U1.D4
  3V3: Part1.3V3, Part3.VCC
  5V: Part1.5V, U1.VCC, R5.Pin_0, R6.leg2
  GND: Part1.GND, Part3.GND, R2.Pin_0, R3.Pin_0, R4.Pin_0, U1.VSS, U1.R/W, U1.LED-, R6.leg1
  N12: J2.pin1, Part2.RESETB
  N13: J2.pin3, Part2.UART_TX
  N14: J2.pin4, Part2.D_DATA
  N15: J1.pin1, Part2.VCC
  N16: J1.pin2, Part2.GND
  N17: J1.pin4, Part2.UART_RX
  N18: J1.pin5, Part2.D_CLOCK
  N19: LED1.anode, R4.Pin_1
  N20: LED2.anode, R3.Pin_1
  N21: LED3.anode, R2.Pin_1
  N22: U1.VO, R6.wiper
  N23: U1.LED+, R5.Pin_1

notes:
  See HM-11_connector.jpg for more indepth connector wiring details
  HM-11 Connector
  HM-11 to Arduino
  220Ω resistors

custom parts:
  LCD-16X2: Standard text-only 16x2 parallel input LCD
