# Fritzing sketch Servo_and_piezo (saved by Fritzing 0.9.3b)
breadboards: 2

parts:
  Part1 = Arduino Uno (Rev3)
  J2 = single row smd female pin header, 4 pins [form="♀ (female)"]
  J1 = single row smd female pin header, 5 pins [form="♀ (female)"]
  Part2 = Bluetooth HM-11
  Part3 = Bluetooth HM-11
  LED1 = LED - 3mm [color="Green (555nm)" package="3 mm [THT]"]
  LED2 = LED - 3mm [color="Blue (430nm)" package="3 mm [THT]"]
  LED3 = LED - 3mm [color="Red (633nm)" package="3 mm [THT]"]
  R2 = Resistor [tolerance=±5% resistance=220 package=THT]
  R3 = Resistor [tolerance=±5% resistance=220 package=THT]
  R4 = Resistor [tolerance=±5% resistance=220 package=THT]
  U1 = LCD-16X2 [package=lcd-16x2]
  R5 = Resistor [tolerance=±5% resistance=220 package=THT]
  R6 = Trimmer Potentiometer [maximum_resistance=10kΩ package=THT]
  J3 = Basic Servo
  100uf-25v_caps_-> = Capacitor Polarized [package=cpol-radial-100uf-25v]
  100uf-25v_caps_->1 = Capacitor Polarized [package=cpol-radial-100uf-25v]
  SP1 = SPEAKER [package=pcb_mount_speaker]

nets:
  N1: Part1.A5/SCL, SP1.-
  N2: Part1.D8, U1.D5
  N3: Part1.D9_PWM, J3.pulse
  N4: Part1.D10_PWM/SS, U1.RS
  N5: Part1.D11_PWM/MOSI, U1.E
  N6: Part1.D12/MISO, U1.D6
  N7: Part1.D13/SCK, U1.D7
  N8: Part1.D2, Part3.UART_TX
  N9: Part1.D3_PWM, Part3.UART_RX
  N10: Part1.D4, LED3.cathode
  N11: Part1.D5_PWM, LED2.cathode
  N12: Part1.D6_PWM, LED1.cathode
  N13: Part1.D7, U1.D4
  3V3: Part1.3V3, Part3.VCC
  VCC: Part1.5V, U1.VCC, R5.Pin_0, R6.leg2, J3.vcc, 100uf-25v_caps_->.+
  GND: Part1.GND, Part3.GND, R2.Pin_0, R3.Pin_0, R4.Pin_0, U1.VSS, U1.R/W, U1.LED-, R6.leg1, J3.gnd, 100uf-25v_caps_->.-, 100uf-25v_caps_->1.-, SP1.+
  N14: J2.pin1, Part2.RESETB
  N15: J2.pin3, Part2.UART_TX
  N16: J2.pin4, Part2.D_DATA
  N17: J1.pin1, Part2.VCC
  N18: J1.pin2, Part2.GND
  N19: J1.pin4, Part2.UART_RX
  N20: J1.pin5, Part2.D_CLOCK
  N21: LED1.anode, R4.Pin_1
  N22: LED2.anode, R3.Pin_1
  N23: LED3.anode, R2.Pin_1
  N24: U1.VO, R6.wiper
  N25: U1.LED+, R5.Pin_1, 100uf-25v_caps_->1.+

notes:
  See HM-11_connector.jpg for more indepth connector wiring details
  HM-11 Connector
  HM-11 to Arduino
  220Ω resistors

custom parts:
  LCD-16X2: Standard text-only 16x2 parallel input LCD
